# Fritzing sketch IR2IP Schematic and PCB Design (saved by Fritzing 0.9.2b)
circuit board: 8.46667cm x 5.64444cm
breadboards: 1

parts:
  Arduino_Board = Arduino Board Ethernet
  IR1 = TSOP312.., 314.. [package=THT]
  LED1 = LEDs [package=led10mm]
  R1 = Resistor [tolerance=±5% resistance=220 package="0603 [SMD]"]

nets:
  N1: Arduino_Board.D2_PWM, R1.Pin_0
  N2: Arduino_Board.D3_PWM, IR1.Data
  N3: Arduino_Board.5V, IR1.Vs
  GND: Arduino_Board.GND, IR1.GND, LED1.A
  N4: LED1.C, R1.Pin_1

notes:
  IR Reciver
  Reciver LED Status
